// Logisim project ALU.circ as structural Verilog
module XOR_NAND (
  input  a,
  input  b,
  output \output 
);

  wire nand_1_out, nand_2_out, nand_3_out;

  nand nand_1 (nand_1_out, a, b, b);
  nand nand_2 (nand_2_out, a, nand_1_out);
  nand nand_3 (nand_3_out, nand_1_out, b);
  nand nand_4 (\output , nand_2_out, nand_3_out);
endmodule

module AND_NAND (
  input  in_1,
  input  in_2,
  output out_3
);

  wire nand_1_out;

  nand nand_1 (nand_1_out, in_1, in_2);
  nand nand_2 (out_3, nand_1_out, nand_1_out);
endmodule

module OR_NAND (
  input  a,
  input  b,
  output \output 
);

  wire nand_1_out, nand_2_out;

  nand nand_1 (nand_1_out, a, a);
  nand nand_2 (nand_2_out, b, b);
  nand nand_3 (\output , nand_1_out, nand_2_out);
endmodule

module NOT_NAND (
  input  a,
  input  b,
  output \output 
);

  wire undriven;

  nand nand_1 (\output , a, undriven);
endmodule

module HALF_ADDER (
  input  a,
  input  in_2,
  output Sum,
  output Varry
);

  wire nand_1_out, nand_2_out, nand_3_out, nand_4_out;

  nand nand_1 (nand_1_out, a, in_2, in_2);
  nand nand_2 (nand_2_out, a, in_2);
  nand nand_3 (nand_3_out, a, nand_1_out);
  nand nand_4 (nand_4_out, nand_1_out, in_2);
  nand nand_5 (Varry, nand_2_out, nand_2_out);
  nand nand_6 (Sum, nand_3_out, nand_4_out);
endmodule

module FULL_ADDER (
  input  a,
  input  b,
  input  c,
  output sum,
  output carry
);

  wire half_adder_1_sum, half_adder_1_varry, half_adder_2_varry;

  HALF_ADDER half_adder_1 (.a(a), .in_2(b), .Sum(half_adder_1_sum), .Varry(half_adder_1_varry));
  HALF_ADDER half_adder_2 (.a(half_adder_1_sum), .in_2(c), .Sum(sum), .Varry(half_adder_2_varry));
  OR_NAND or_nand_1 (.a(half_adder_2_varry), .b(half_adder_1_varry), .\output (carry));
endmodule

module ALU (
  input  [15:0] x,
  input  zx,
  input  nx,
  input  no,
  input  [15:0] y,
  input  zy,
  input  ny,
  input  f,
  output [15:0] out,
  output zero,
  output negative
);

  wire or_1_out;
  wire [15:0] adder_1_out, and_1_out, multiplexer_1_out, multiplexer_2_out, multiplexer_3_out,
       multiplexer_4_out, multiplexer_5_out, not_1_out, not_2_out, not_4_out;

  Multiplexer #(.width(16)) multiplexer_1 (.in0(x), .in1({16{1'b0}}), .out(multiplexer_1_out), .sel(zx));  // open: en
  assign not_1_out = ~multiplexer_1_out;  // NOT_Gate not_1, 16 bits wide
  Multiplexer #(.width(16)) multiplexer_2 (.in0(y), .in1({16{1'b0}}), .out(multiplexer_2_out), .sel(zy));  // open: en
  assign not_2_out = ~multiplexer_2_out;  // NOT_Gate not_2, 16 bits wide
  Multiplexer #(.width(16)) multiplexer_3 (
    .in0(multiplexer_1_out), .in1(not_1_out), .out(multiplexer_3_out), .sel(nx));  // open: en
  Multiplexer #(.width(16)) multiplexer_4 (
    .in0(multiplexer_2_out), .in1(not_2_out), .out(multiplexer_4_out), .sel(ny));  // open: en
  or or_1 (or_1_out, out[0], out[1], out[2], out[3], out[4], out[5], out[6], out[7], out[8], out[9], out[11], out[12], out[10], out[13], out[14], negative);
  not not_3 (zero, or_1_out);
  assign and_1_out = multiplexer_3_out & multiplexer_4_out;  // AND_Gate and_1, 16 bits wide
  Adder #(.width(16)) adder_1 (
    .a(multiplexer_3_out), .b(multiplexer_4_out), .out(adder_1_out), .cin(1'b0));  // open: cout
  Multiplexer #(.width(16)) multiplexer_5 (
    .in0(and_1_out), .in1(adder_1_out), .out(multiplexer_5_out), .sel(f));  // open: en
  assign not_4_out = ~multiplexer_5_out;  // NOT_Gate not_4, 16 bits wide
  Multiplexer #(.width(16)) multiplexer_6 (
    .in0(multiplexer_5_out), .in1(not_4_out), .out({negative, out[14:0]}), .sel(no));  // open: en

  assign out[15] = negative;
endmodule
