// Logisim project NOT-NAND.circ as structural Verilog: 1 circuit, main circuit main
module main (
  input  a,
  input  b,
  output \output 
);

  wire undriven;

  nand nand_1 (\output , a, undriven);
endmodule
