// Logisim project XOR-NAND.circ as structural Verilog: 1 circuit, main circuit main
module main (
  input  a,
  input  b,
  output \output 
);

  wire nand_1_out, nand_2_out, nand_3_out;

  nand nand_1 (nand_1_out, a, b, b);
  nand nand_2 (nand_2_out, a, nand_1_out);
  nand nand_3 (nand_3_out, nand_1_out, b);
  nand nand_4 (\output , nand_2_out, nand_3_out);
endmodule
