// Logisim project cpu.circ as structural Verilog
module XOR_NAND (
  input  a,
  input  b,
  output \output 
);

  wire nand_1_out, nand_2_out, nand_3_out;

  nand nand_1 (nand_1_out, a, b, b);
  nand nand_2 (nand_2_out, a, nand_1_out);
  nand nand_3 (nand_3_out, nand_1_out, b);
  nand nand_4 (\output , nand_2_out, nand_3_out);
endmodule

module AND_NAND (
  input  in_1,
  input  in_2,
  output out_3
);

  wire nand_1_out;

  nand nand_1 (nand_1_out, in_1, in_2);
  nand nand_2 (out_3, nand_1_out, nand_1_out);
endmodule

module OR_NAND (
  input  a,
  input  b,
  output \output 
);

  wire nand_1_out, nand_2_out;

  nand nand_1 (nand_1_out, a, a);
  nand nand_2 (nand_2_out, b, b);
  nand nand_3 (\output , nand_1_out, nand_2_out);
endmodule

module NOT_NAND (
  input  a,
  input  b,
  output \output 
);

  wire undriven;

  nand nand_1 (\output , a, undriven);
endmodule
